// Logisim project CPU.circ as structural Verilog: 1 circuit, main circuit main
module main (
);

  wire AD, adder_1_cout, AN, and_2_out, and_3_out, CE, CF, CLK, clock_1_out, controlled_buffer_16_out,
       controlled_buffer_19_out, controlled_buffer_29_out, controlled_buffer_30_out, CR, CRRY,
       decoder_2_out0, DI, EI, EO, IR, J, MU, not_1_out, not_3_out, NT, RA, RB, RC, RE, RF, RM, RO, RST, ST,
       SU, subtractor_1_bout, WA, WB, WC, WD, WE, WI, WM, WR, WX, WY, X_carry;
  wire [0:0] decoder_1_out0;
  wire [1:0] FLAGS;
  wire [1:1] FLGS;
  wire [3:0] rom_1_data_2;
  wire [7:0] controlled_buffer_13_out;
  wire [13:0] ROM_ADDR;
  wire [15:0] adder_1_out, ALU, and_1_out, controlled_buffer_2_out, controlled_buffer_3_out,
       controlled_buffer_4_out, controlled_buffer_7_out, controlled_buffer_8_out, controlled_buffer_9_out,
       controlled_buffer_12_out, controlled_buffer_17_out, DATABUS, decoder_3_out0, DISPLY, divider_1_out,
       multiplier_1_out, not_2_out, or_1_out, PRGM_CTR, ram_1_dout, RAM_ADDR, regA, regB, regC, regE,
       rom_1_data, subtractor_1_out, Y_q;
  wire [15:2] pull_resistor_9_node;
  wire [15:12] decoder_2_out12;
  wire [15:14] pull_resistor_8_node;

  Clock clock_1 (.out(clock_1_out));
  not not_1 (not_1_out, ST);
  DotMatrix #(.matrixcols(16), .matrixrows(1)) dotmatrix_1 (
    .col0(regA[15]), .col1(regA[14]), .col2(regA[13]), .col3(regA[12]), .col4(regA[11]), .col5(regA[10]),
    .col6(regA[9]), .col7(regA[8]), .col8(regA[7]), .col9(regA[6]), .col10(regA[5]), .col11(regA[4]),
    .col12(regA[3]), .col13(regA[2]), .col14(regA[1]), .col15(regA[0]));
  DotMatrix #(.matrixcols(16), .matrixrows(1)) dotmatrix_2 (
    .col0(regB[15]), .col1(regB[14]), .col2(regB[13]), .col3(regB[12]), .col4(regB[11]), .col5(regB[10]),
    .col6(regB[9]), .col7(regB[8]), .col8(regB[7]), .col9(regB[6]), .col10(regB[5]), .col11(regB[4]),
    .col12(regB[3]), .col13(regB[2]), .col14(regB[1]), .col15(regB[0]));
  DotMatrix #(.matrixcols(16), .matrixrows(1)) dotmatrix_3 (
    .col0(regC[15]), .col1(regC[14]), .col2(regC[13]), .col3(regC[12]), .col4(regC[11]), .col5(regC[10]),
    .col6(regC[9]), .col7(regC[8]), .col8(regC[7]), .col9(regC[6]), .col10(regC[5]), .col11(regC[4]),
    .col12(regC[3]), .col13(regC[2]), .col14(regC[1]), .col15(regC[0]));
  DotMatrix #(.matrixcols(16), .matrixrows(1)) dotmatrix_4 (
    .col0(regE[15]), .col1(regE[14]), .col2(regE[13]), .col3(regE[12]), .col4(regE[11]), .col5(regE[10]),
    .col6(regE[9]), .col7(regE[8]), .col8(regE[7]), .col9(regE[6]), .col10(regE[5]), .col11(regE[4]),
    .col12(regE[3]), .col13(regE[2]), .col14(regE[1]), .col15(regE[0]));
  DotMatrix #(.matrixcols(16), .matrixrows(1)) dotmatrix_5 (
    .col0(RAM_ADDR[15]), .col1(RAM_ADDR[14]), .col2(RAM_ADDR[13]), .col3(RAM_ADDR[12]), .col4(RAM_ADDR[11]),
    .col5(RAM_ADDR[10]), .col6(RAM_ADDR[9]), .col7(RAM_ADDR[8]), .col8(RAM_ADDR[7]), .col9(RAM_ADDR[6]),
    .col10(RAM_ADDR[5]), .col11(RAM_ADDR[4]), .col12(RAM_ADDR[3]), .col13(RAM_ADDR[2]), .col14(RAM_ADDR[1]),
    .col15(RAM_ADDR[0]));
  DotMatrix #(.matrixcols(16), .matrixrows(1)) dotmatrix_6 (
    .col0(pull_resistor_8_node[15]), .col1(pull_resistor_8_node[14]), .col2(ROM_ADDR[13]),
    .col3(ROM_ADDR[12]), .col4(ROM_ADDR[11]), .col5(ROM_ADDR[10]), .col6(ROM_ADDR[9]), .col7(ROM_ADDR[8]),
    .col8(ROM_ADDR[7]), .col9(ROM_ADDR[6]), .col10(ROM_ADDR[5]), .col11(ROM_ADDR[4]), .col12(ROM_ADDR[3]),
    .col13(ROM_ADDR[2]), .col14(ROM_ADDR[1]), .col15(ROM_ADDR[0]));
  DotMatrix #(.matrixcols(16), .matrixrows(1)) dotmatrix_7 (
    .col0(pull_resistor_9_node[15]), .col1(pull_resistor_9_node[14]), .col2(pull_resistor_9_node[13]),
    .col3(pull_resistor_9_node[12]), .col4(pull_resistor_9_node[11]), .col5(pull_resistor_9_node[10]),
    .col6(pull_resistor_9_node[9]), .col7(pull_resistor_9_node[8]), .col8(pull_resistor_9_node[7]),
    .col9(pull_resistor_9_node[6]), .col10(pull_resistor_9_node[5]), .col11(pull_resistor_9_node[4]),
    .col12(pull_resistor_9_node[3]), .col13(pull_resistor_9_node[2]), .col14(FLAGS[1]), .col15(FLAGS[0]));
  DotMatrix #(.matrixcols(16), .matrixrows(1)) dotmatrix_8 (
    .col0(ALU[15]), .col1(ALU[14]), .col2(ALU[13]), .col3(ALU[12]), .col4(ALU[11]), .col5(ALU[10]),
    .col6(ALU[9]), .col7(ALU[8]), .col8(ALU[7]), .col9(ALU[6]), .col10(ALU[5]), .col11(ALU[4]),
    .col12(ALU[3]), .col13(ALU[2]), .col14(ALU[1]), .col15(ALU[0]));
  DotMatrix #(.matrixcols(16), .matrixrows(1)) dotmatrix_9 (
    .col0(PRGM_CTR[15]), .col1(PRGM_CTR[14]), .col2(PRGM_CTR[13]), .col3(PRGM_CTR[12]), .col4(PRGM_CTR[11]),
    .col5(PRGM_CTR[10]), .col6(PRGM_CTR[9]), .col7(PRGM_CTR[8]), .col8(PRGM_CTR[7]), .col9(PRGM_CTR[6]),
    .col10(PRGM_CTR[5]), .col11(PRGM_CTR[4]), .col12(PRGM_CTR[3]), .col13(PRGM_CTR[2]), .col14(PRGM_CTR[1]),
    .col15(PRGM_CTR[0]));
  DotMatrix #(.matrixcols(16), .matrixrows(1)) dotmatrix_10 (
    .col0(DATABUS[15]), .col1(DATABUS[14]), .col2(DATABUS[13]), .col3(DATABUS[12]), .col4(DATABUS[11]),
    .col5(DATABUS[10]), .col6(DATABUS[9]), .col7(DATABUS[8]), .col8(DATABUS[7]), .col9(DATABUS[6]),
    .col10(DATABUS[5]), .col11(DATABUS[4]), .col12(DATABUS[3]), .col13(DATABUS[2]), .col14(DATABUS[1]),
    .col15(DATABUS[0]));
  Pull_Resistor pull_resistor_1 (.node(RST));
  Pull_Resistor pull_resistor_2 (.node(CLK));
  assign CLK = not_1_out ? clock_1_out : 1'bz;  // Controlled_Buffer controlled_buffer_1
  Button button_1 (.out(RST));
  Pull_Resistor pull_resistor_3 (.node(regA));
  Pull_Resistor pull_resistor_4 (.node(regB));
  Pull_Resistor pull_resistor_5 (.node(regC));
  Pull_Resistor pull_resistor_6 (.node(regE));
  Pull_Resistor pull_resistor_7 (.node(RAM_ADDR));
  Pull_Resistor pull_resistor_8 (.node({pull_resistor_8_node, ROM_ADDR}));
  Pull_Resistor pull_resistor_9 (.node({pull_resistor_9_node, FLAGS}));
  Pull_Resistor pull_resistor_10 (.node(ALU));
  Pull_Resistor pull_resistor_11 (.node(PRGM_CTR));
  Pull_Resistor pull_resistor_12 (.node(DATABUS));
  Register #(.width(16)) A (.D(controlled_buffer_2_out), .en(WA), .clk(CLK), .Q(regA), .clr(RST));
  assign controlled_buffer_2_out = WA ? DATABUS : 16'bz;  // Controlled_Buffer controlled_buffer_2
  Register #(.width(16)) C (.D(controlled_buffer_3_out), .en(WC), .clk(CLK), .Q(regC), .clr(RST));
  assign controlled_buffer_3_out = WC ? DATABUS : 16'bz;  // Controlled_Buffer controlled_buffer_3
  assign controlled_buffer_4_out = WX ? DATABUS : 16'bz;  // Controlled_Buffer controlled_buffer_4
  Counter #(.max('hffff), .width(16)) X (
    .load(WX), .D(controlled_buffer_4_out), .carry(X_carry), .clk(CLK));  // open: count, Q, up, clr
  assign DATABUS = RA ? regA : 16'bz;  // Controlled_Buffer controlled_buffer_5
  assign DATABUS = RC ? regC : 16'bz;  // Controlled_Buffer controlled_buffer_6
  assign controlled_buffer_7_out = WY ? DATABUS : 16'bz;  // Controlled_Buffer controlled_buffer_7
  Counter #(.max('hffff), .width(16)) Y (
    .load(WY), .D(controlled_buffer_7_out), .count(X_carry), .Q(Y_q), .clk(CLK));  // open: carry, up, clr
  Register #(.width(16)) B (.D(controlled_buffer_8_out), .en(WB), .clk(CLK), .Q(regB), .clr(RST));
  assign controlled_buffer_8_out = WB ? DATABUS : 16'bz;  // Controlled_Buffer controlled_buffer_8
  Register #(.width(16)) EXPANSION (.D(controlled_buffer_9_out), .en(WE), .clk(CLK), .Q(regE), .clr(RST));
  assign controlled_buffer_9_out = WE ? DATABUS : 16'bz;  // Controlled_Buffer controlled_buffer_9
  // RGB_Video #(.cursor("No Cursor"), .height(256), .scale(1), .width(256)) rgb_video_1: pin names not known; wires that end beside it: WX, WY, RST, CLK, 1'b1, DISPLY[7:0]
  assign DATABUS = RB ? regB : 16'bz;  // Controlled_Buffer controlled_buffer_10
  assign DATABUS = RE ? regE : 16'bz;  // Controlled_Buffer controlled_buffer_11
  Register #(.width(16)) DISPLAY (.D(controlled_buffer_12_out), .en(WD), .clk(CLK), .Q(DISPLY), .clr(RST));
  assign controlled_buffer_12_out = WD ? DATABUS : 16'bz;  // Controlled_Buffer controlled_buffer_12
  Register INSTR (.D(controlled_buffer_13_out), .en(WI), .clk(CLK), .Q(ROM_ADDR[11:4]), .clr(RST));
  assign controlled_buffer_13_out = WI ? DATABUS[7:0] : 8'bz;  // Controlled_Buffer controlled_buffer_13
  assign DATABUS = CR ? PRGM_CTR : 16'bz;  // Controlled_Buffer controlled_buffer_14
  Counter #(.max('hffff), .width(16)) PC (
    .load(J), .D(DATABUS), .count(CE), .Q(PRGM_CTR), .clk(CLK), .clr(RST));  // open: carry, up
  assign DATABUS[7:0] = IR ? ROM_ADDR[11:4] : 8'bz;  // Controlled_Buffer controlled_buffer_15
  assign controlled_buffer_16_out = RST ? RST : 1'bz;  // Controlled_Buffer controlled_buffer_16
  assign not_2_out = ~regA;  // NOT_Gate not_2, 16 bits wide
  assign and_1_out = regA & regB;  // AND_Gate and_1, 16 bits wide
  assign or_1_out = regA | regB;  // OR_Gate or_1, 16 bits wide
  Divider #(.width(16)) divider_1 (.a(regA), .b(regB), .out(divider_1_out));  // open: upper, rem
  Multiplier #(.width(16)) multiplier_1 (.a(regA), .b(regB), .out(multiplier_1_out));  // open: cin, cout
  Adder #(.width(16)) adder_1 (.a(regA), .b(regB), .out(adder_1_out), .cout(adder_1_cout));  // open: cin
  Subtractor #(.width(16)) subtractor_1 (
    .a(regA), .b(regB), .out(subtractor_1_out), .bout(subtractor_1_bout));  // open: bin
  Register #(.width(16)) MAR (.D(controlled_buffer_17_out), .en(WR), .clk(CLK), .Q(RAM_ADDR), .clr(RST));
  assign controlled_buffer_17_out = WR ? DATABUS : 16'bz;  // Controlled_Buffer controlled_buffer_17
  Register #(.width(2)) u_FLAGS (.D({FLGS[1], CRRY}), .en(1'b1), .clk(CLK), .Q(FLAGS), .clr(controlled_buffer_16_out));
  assign controlled_buffer_16_out = CF ? CF : 1'bz;  // Controlled_Buffer controlled_buffer_18
  Pull_Resistor pull_resistor_13 (.node(controlled_buffer_16_out));
  assign controlled_buffer_19_out = RST ? RST : 1'bz;  // Controlled_Buffer controlled_buffer_19
  Counter #(.max('hf), .width(4)) SC (
    .load(1'b0), .count(1'b1), .Q(ROM_ADDR[3:0]), .clk(not_3_out), .clr(controlled_buffer_19_out));  // open: D, carry, up
  not not_3 (not_3_out, CLK);
  Pull_Resistor pull_resistor_14 (.node(controlled_buffer_19_out));
  assign controlled_buffer_19_out = EI ? EI : 1'bz;  // Controlled_Buffer controlled_buffer_20
  assign ALU = NT ? not_2_out : 16'bz;  // Controlled_Buffer controlled_buffer_21
  assign DATABUS = EO ? ALU : 16'bz;  // Controlled_Buffer controlled_buffer_22
  Pull_Resistor pull_resistor_15 (.node(ALU));
  assign ALU = AN ? and_1_out : 16'bz;  // Controlled_Buffer controlled_buffer_23
  assign ALU = RO ? or_1_out : 16'bz;  // Controlled_Buffer controlled_buffer_24
  assign ALU = DI ? divider_1_out : 16'bz;  // Controlled_Buffer controlled_buffer_25
  assign ALU = MU ? multiplier_1_out : 16'bz;  // Controlled_Buffer controlled_buffer_26
  assign ALU = AD ? adder_1_out : 16'bz;  // Controlled_Buffer controlled_buffer_27
  assign ALU = SU ? subtractor_1_out : 16'bz;  // Controlled_Buffer controlled_buffer_28
  assign controlled_buffer_29_out = AD ? adder_1_cout : 1'bz;  // Controlled_Buffer controlled_buffer_29
  assign controlled_buffer_30_out = SU ? subtractor_1_bout : 1'bz;  // Controlled_Buffer controlled_buffer_30
  RAM #(.addrWidth(16), .dataWidth(16), .trigger("high")) ram_1 (
    .addr(RAM_ADDR), .we(WM), .oe(RM), .din(DATABUS), .dout(ram_1_dout));
  Pull_Resistor pull_resistor_16 (.node(RF));
  ROM #(.addrWidth(14), .dataWidth(16)) rom_1 (
    .addr(ROM_ADDR), .data({rom_1_data[15], CF, EI, ST, CE, rom_1_data[10:8], rom_1_data_2, rom_1_data[3:0]}));
  assign ROM_ADDR[13:12] = RF ? FLAGS : 2'bz;  // Controlled_Buffer controlled_buffer_31
  Pull_Resistor pull_resistor_17 (.node(ROM_ADDR));
  nor nor_1 (FLGS[1], ALU[0], ALU[1], ALU[2], ALU[3], ALU[4], ALU[5], ALU[6], ALU[7], ALU[9], ALU[10], ALU[11], ALU[12], ALU[13], ALU[14], ALU[15], ALU[8]);
  and and_2 (and_2_out, AD, controlled_buffer_29_out);
  assign CRRY = AD ? and_2_out : 1'bz;  // Controlled_Buffer controlled_buffer_32
  Pull_Resistor pull_resistor_18 (.node(CRRY));
  and and_3 (and_3_out, controlled_buffer_30_out, SU);
  assign CRRY = SU ? and_3_out : 1'bz;  // Controlled_Buffer controlled_buffer_33
  Decoder #(.enable("false"), .select(3)) decoder_1 (
    .out0(decoder_1_out0[0]), .out1(AD), .out2(SU), .out3(MU), .out4(DI), .out5(AN), .out6(RO), .out7(NT),
    .sel(rom_1_data[10:8]));
  Decoder #(.enable("false"), .select(4)) decoder_2 (
    .out0(decoder_2_out0), .out1(WA), .out2(WB), .out3(WC), .out4(WE), .out5(WM), .out6(WI), .out7(WR),
    .out8(J), .out9(WD), .out10(WX), .out11(WY), .out12(decoder_2_out12[12]), .out13(decoder_2_out12[13]),
    .out14(decoder_2_out12[14]), .out15(decoder_2_out12[15]), .sel(rom_1_data_2));
  assign DATABUS = RM ? ram_1_dout : 16'bz;  // Controlled_Buffer controlled_buffer_34
  Decoder #(.enable("false"), .select(4)) decoder_3 (
    .out0(decoder_3_out0[0]), .out1(RA), .out2(RB), .out3(RC), .out4(RE), .out5(RM), .out6(IR), .out7(CR),
    .out8(EO), .out9(RF), .out10(decoder_3_out0[10]), .out11(decoder_3_out0[11]), .out12(decoder_3_out0[12]),
    .out13(decoder_3_out0[13]), .out14(decoder_3_out0[14]), .out15(decoder_3_out0[15]), .sel(rom_1_data[3:0]));

  // Other names for the same wires on the sheet: FLGS[0] = CRRY; ZERO = FLGS[1]

  // Notes on the sheet:
  //   contents of rom_1 (hex, n*v repeats v):
  //   77 865 2000 13*0 77 865 77 875 15 2000 10*0 77 865 77 875 25 2000 10*0 77 865 77 875 35 2000 10*0 77
  //   865 77 815 2000 11*0 77 865 77 825 2000 11*0 77 865 14 2000 12*0 77 865 41 2000 12*0 77 865 77 875
  //   51 2000 10*0 77 865 77 875 53 2000 10*0 77 865 118 2000 12*0 77 865 218 2000 12*0 77 865 318 2000
  //   12*0 77 865 418 2000 12*0 77 865 77 885 2000 11*0 77 865 9 800 2000 11*0 77 865 9 800 2000 11*0 77
  //   865 71 15 2000 11*0 77 865 71 52 2000 11*0 77 865 32 21 13 2000 10*0 77 865 23 31 12 2000 10*0 77
  //   865 1000 13*0 77 865 91 2000 12*0 77 865 a1 2000 14*0 b1 2000 3951*0 800 2000 14*0 77 85 77 6000
  //   4076*0 77 85 77 6000 12*0 800 2000 4078*0 77 85 77 6000 12*0 77 85 77 6000
endmodule
